# Fritzing sketch schemat (saved by Fritzing 0.9.3b)
breadboards: 1

parts:
  BeagleBone1 = BeagleBone Black
  S1 = Pushbutton [package="[SMD]"]
  S2 = Pushbutton [package="[SMD]"]
  S3 = Pushbutton [package="[SMD]"]
  S4 = Pushbutton [package="[SMD]"]
  R1 = Resistor [tolerance=±5% resistance=1k package=THT]
  R2 = Resistor [tolerance=±5% resistance=1k package=THT]
  R3 = Resistor [tolerance=±5% resistance=1k package=THT]
  R4 = Resistor [tolerance=±5% resistance=1k package=THT]
  LED9 = smd LED [color="Green (555nm)" package="0805 [SMD]"]
  LED10 = smd LED [color="Green (555nm)" package="0805 [SMD]"]
  LED11 = smd LED [color="Green (555nm)" package="0805 [SMD]"]
  LED12 = smd LED [color="Green (555nm)" package="0805 [SMD]"]
  J1 = Piezo Speaker
  IC1 = DS1307 [package=THT]

nets:
  N1: BeagleBone1.no_name_yet#1, R1.Pin_1, R2.Pin_1, R3.Pin_1, R4.Pin_1
  N2: BeagleBone1.no_name_yet#2, IC1.0V
  N3: BeagleBone1.no_name_yet#7, S1.Pin_1, S1.Pin_2, S2.Pin_1, S2.Pin_2, S3.Pin_1, S3.Pin_2, S4.Pin_1, S4.Pin_2, LED9.cathode, LED10.cathode, LED11.cathode, LED12.cathode, J1.pin2
  N4: BeagleBone1.no_name_yet#8, IC1.+V
  N5: BeagleBone1.no_name_yet#19, IC1.SCL_-_I2C_Clock
  N6: BeagleBone1.no_name_yet#20, IC1.SDA_-_I2C_Data
  N7: BeagleBone1.no_name_yet#107, LED9.anode
  N8: BeagleBone1.no_name_yet#108, S1.Pin_3, S1.Pin_4, R1.Pin_0
  N9: BeagleBone1.no_name_yet#109, LED10.anode
  N10: BeagleBone1.no_name_yet#110, S2.Pin_3, S2.Pin_4, R2.Pin_0
  N11: BeagleBone1.no_name_yet#111, LED11.anode
  N12: BeagleBone1.no_name_yet#112, S3.Pin_3, S3.Pin_4, R3.Pin_0
  N13: BeagleBone1.no_name_yet#115, LED12.anode
  N14: BeagleBone1.no_name_yet#116, S4.Pin_3, S4.Pin_4, R4.Pin_0

custom parts:
  BeagleBone Black: BeagleBone Black rev. A5B
